// Logisim project Digital CLOCK (FINAL).circ as structural Verilog: 8 circuits, main circuit CLOCK\
module CLOCK (
);

  wire frame_1_a, frame_1_b, frame_1_c, frame_1_d, frame_1_e, frame_1_f, frame_1_g, frame_1_out_6,
       frame_1_out_7, frame_1_out_8, frame_1_out_9, frame_1_out_10, frame_1_out_11, frame_1_out_12,
       frame_1_out_13, frame_1_out_14, frame_1_out_15, frame_1_out_16, frame_1_out_17, frame_1_out_18,
       frame_1_out_19, frame_1_out_20, frame_1_out_21, frame_1_out_22, frame_1_out_23, frame_1_out_24,
       frame_1_out_25, frame_1_out_26, frame_1_out_27, frame_1_out_28, frame_1_out_29, frame_1_out_30,
       frame_1_out_31, frame_1_out_32, frame_1_out_33, frame_1_out_34, frame_1_out_35, frame_1_out_36,
       frame_1_out_37, frame_1_out_38, frame_1_out_39, frame_1_out_40, H_out, M_2_out, M_out, S_2_out, S_out;
  wire [6:0] frame_1_out_48, frame_1_out_49, frame_1_out_50, frame_1_out_51, frame_1_out_52, frame_1_out_53,
       frame_1_out_54, frame_1_out_55, frame_1_out_56, frame_1_out_57, frame_1_out_58, frame_1_out_59,
       frame_1_out_60, frame_1_out_61;

  DotMatrix dotmatrix_1 (
    .col0(frame_1_out_57), .col1(frame_1_out_58), .col2(frame_1_out_59), .col3(frame_1_out_60),
    .col4(frame_1_out_61));
  DotMatrix #(.matrixcols(9)) dotmatrix_2 (
    .col0(frame_1_out_48), .col1(frame_1_out_49), .col2(frame_1_out_50), .col3(frame_1_out_51),
    .col4(frame_1_out_52), .col5(frame_1_out_53), .col6(frame_1_out_54), .col7(frame_1_out_55),
    .col8(frame_1_out_56));
  _7_Segment_Display u_7_segment_display_1 (
    .g(frame_1_out_12), .f(frame_1_out_11), .a(frame_1_out_6), .b(frame_1_out_7), .e(frame_1_out_10),
    .d(frame_1_out_9), .c(frame_1_out_8));  // open: dp
  _7_Segment_Display u_7_segment_display_2 (
    .g(frame_1_out_19), .f(frame_1_out_18), .a(frame_1_out_13), .b(frame_1_out_14), .e(frame_1_out_17),
    .d(frame_1_out_16), .c(frame_1_out_15));  // open: dp
  Button H (.out(H_out));
  _7_Segment_Display u_7_segment_display_3 (
    .g(frame_1_out_33), .f(frame_1_out_32), .a(frame_1_out_27), .b(frame_1_out_28), .e(frame_1_out_31),
    .d(frame_1_out_30), .c(frame_1_out_29));  // open: dp
  _7_Segment_Display u_7_segment_display_4 (
    .g(frame_1_out_26), .f(frame_1_out_25), .a(frame_1_out_20), .b(frame_1_out_21), .e(frame_1_out_24),
    .d(frame_1_out_23), .c(frame_1_out_22));  // open: dp
  Button M (.out(M_out));
  _7_Segment_Display u_7_segment_display_5 (
    .g(frame_1_out_40), .f(frame_1_out_39), .a(frame_1_out_34), .b(frame_1_out_35), .e(frame_1_out_38),
    .d(frame_1_out_37), .c(frame_1_out_36));  // open: dp
  Button S (.out(S_out));
  Button M_2 (.out(M_2_out));
  Frame frame_1 (
    .in_1(H_out), .in_2(M_out), .in_3(M_2_out), .in_4(S_out), .in_5(S_2_out), .out_6(frame_1_out_6),
    .out_7(frame_1_out_7), .out_8(frame_1_out_8), .out_9(frame_1_out_9), .out_10(frame_1_out_10),
    .out_11(frame_1_out_11), .out_12(frame_1_out_12), .out_13(frame_1_out_13), .out_14(frame_1_out_14),
    .out_15(frame_1_out_15), .out_16(frame_1_out_16), .out_17(frame_1_out_17), .out_18(frame_1_out_18),
    .out_19(frame_1_out_19), .out_20(frame_1_out_20), .out_21(frame_1_out_21), .out_22(frame_1_out_22),
    .out_23(frame_1_out_23), .out_24(frame_1_out_24), .out_25(frame_1_out_25), .out_26(frame_1_out_26),
    .out_27(frame_1_out_27), .out_28(frame_1_out_28), .out_29(frame_1_out_29), .out_30(frame_1_out_30),
    .out_31(frame_1_out_31), .out_32(frame_1_out_32), .out_33(frame_1_out_33), .out_34(frame_1_out_34),
    .out_35(frame_1_out_35), .out_36(frame_1_out_36), .out_37(frame_1_out_37), .out_38(frame_1_out_38),
    .out_39(frame_1_out_39), .out_40(frame_1_out_40), .a(frame_1_a), .b(frame_1_b), .c(frame_1_c),
    .d(frame_1_d), .e(frame_1_e), .f(frame_1_f), .g(frame_1_g), .out_61(frame_1_out_61),
    .out_60(frame_1_out_60), .out_59(frame_1_out_59), .out_58(frame_1_out_58), .out_57(frame_1_out_57),
    .out_52(frame_1_out_52), .out_53(frame_1_out_53), .out_54(frame_1_out_54), .out_55(frame_1_out_55),
    .out_56(frame_1_out_56), .out_48(frame_1_out_48), .out_49(frame_1_out_49), .out_50(frame_1_out_50),
    .out_51(frame_1_out_51));
  _7_Segment_Display u_7_segment_display_6 (
    .g(frame_1_g), .f(frame_1_f), .a(frame_1_a), .b(frame_1_b), .e(frame_1_e), .d(frame_1_d), .c(frame_1_c));  // open: dp
  Button S_2 (.out(S_2_out));

  // Notes on the sheet:
  //   PRESS THE BUTTONS TO SET THE CLOCK
  //   THEN ENABLE AUTO CLOCK TICKS
  //   "WITH GREETING FROM ALL THE TEAM MEMBERS"
endmodule

module Frame (
  input  in_1,
  input  in_2,
  input  in_3,
  input  in_4,
  input  in_5,
  output out_6,
  output out_7,
  output out_8,
  output out_9,
  output out_10,
  output out_11,
  output out_12,
  output out_13,
  output out_14,
  output out_15,
  output out_16,
  output out_17,
  output out_18,
  output out_19,
  output out_20,
  output out_21,
  output out_22,
  output out_23,
  output out_24,
  output out_25,
  output out_26,
  output out_27,
  output out_28,
  output out_29,
  output out_30,
  output out_31,
  output out_32,
  output out_33,
  output out_34,
  output out_35,
  output out_36,
  output out_37,
  output out_38,
  output out_39,
  output out_40,
  output a,
  output b,
  output c,
  output d,
  output e,
  output f,
  output g,
  output [6:0] out_48,
  output [6:0] out_49,
  output [6:0] out_50,
  output [6:0] out_51,
  output [6:0] out_52,
  output [6:0] out_53,
  output [6:0] out_54,
  output [6:0] out_55,
  output [6:0] out_56,
  output [6:0] out_57,
  output [6:0] out_58,
  output [6:0] out_59,
  output [6:0] out_60,
  output [6:0] out_61
);

  wire clock_1_out, h_counter_1_lb0, h_counter_1_lb1, h_counter_1_lb2, h_counter_1_lb3, h_counter_1_rb0,
       h_counter_1_rb1, h_counter_1_rb2, h_counter_1_rb3, l_counter_1_overflow, l_counter_1_q0,
       l_counter_1_q1, l_counter_1_q2, l_counter_1_q3, l_counter_2_overflow, l_counter_2_q0, l_counter_2_q1,
       l_counter_2_q2, l_counter_2_q3, r_counter_1_overflow, r_counter_1_q0, r_counter_1_q1, r_counter_1_q2,
       r_counter_1_q3, r_counter_2_overflow, r_counter_2_q0, r_counter_2_q1, r_counter_2_q2, r_counter_2_q3;

  SEG_DECD seg_decd_1 (
    .a(out_6), .b(out_7), .c(out_8), .d(out_9), .e(out_10), .f(out_11), .g(out_12), .b2(h_counter_1_lb2),
    .b1(h_counter_1_lb1), .b0(h_counter_1_lb0), .b3(h_counter_1_lb3));
  H_Counter h_counter_1 (
    .Lb0(h_counter_1_lb0), .Rb0(h_counter_1_rb0), .Lb1(h_counter_1_lb1), .Rb1(h_counter_1_rb1),
    .Lb2(h_counter_1_lb2), .Rb2(h_counter_1_rb2), .Lb3(h_counter_1_lb3), .Rb3(h_counter_1_rb3),
    .clock(l_counter_1_overflow), .SET(in_1), .am_pm(out_61[2]));
  SEG_DECD seg_decd_2 (
    .a(out_13), .b(out_14), .c(out_15), .d(out_16), .e(out_17), .f(out_18), .g(out_19), .b2(h_counter_1_rb2),
    .b1(h_counter_1_rb1), .b0(h_counter_1_rb0), .b3(h_counter_1_rb3));
  SEG_DECD seg_decd_3 (
    .a(out_20), .b(out_21), .c(out_22), .d(out_23), .e(out_24), .f(out_25), .g(out_26), .b2(l_counter_1_q2),
    .b1(l_counter_1_q1), .b0(l_counter_1_q0), .b3(l_counter_1_q3));
  SEG_DECD seg_decd_4 (
    .a(out_27), .b(out_28), .c(out_29), .d(out_30), .e(out_31), .f(out_32), .g(out_33), .b2(r_counter_1_q2),
    .b1(r_counter_1_q1), .b0(r_counter_1_q0), .b3(r_counter_1_q3));
  L_counter l_counter_1 (
    .Q3(l_counter_1_q3), .Q2(l_counter_1_q2), .Q1(l_counter_1_q1), .Q0(l_counter_1_q0),
    .overflow(l_counter_1_overflow), .in_1(r_counter_1_overflow), .in_2(in_2));
  R_counter r_counter_1 (
    .Q3(r_counter_1_q3), .Q2(r_counter_1_q2), .Q1(r_counter_1_q1), .Q0(r_counter_1_q0),
    .overflow(r_counter_1_overflow), .in_1(in_3), .in_2(l_counter_2_overflow));
  SEG_DECD seg_decd_5 (
    .a(out_34), .b(out_35), .c(out_36), .d(out_37), .e(out_38), .f(out_39), .g(out_40), .b2(l_counter_2_q2),
    .b1(l_counter_2_q1), .b0(l_counter_2_q0), .b3(l_counter_2_q3));
  SEG_DECD seg_decd_6 (
    .a(a), .b(b), .c(c), .d(d), .e(e), .f(f), .g(g), .b2(r_counter_2_q2), .b1(r_counter_2_q1),
    .b0(r_counter_2_q0), .b3(r_counter_2_q3));
  L_counter l_counter_2 (
    .Q3(l_counter_2_q3), .Q2(l_counter_2_q2), .Q1(l_counter_2_q1), .Q0(l_counter_2_q0),
    .overflow(l_counter_2_overflow), .in_1(r_counter_2_overflow), .in_2(in_4));
  R_counter r_counter_2 (
    .Q3(r_counter_2_q3), .Q2(r_counter_2_q2), .Q1(r_counter_2_q1), .Q0(r_counter_2_q0),
    .overflow(r_counter_2_overflow), .in_1(in_5), .in_2(clock_1_out));
  Clock clock_1 (.out(clock_1_out));

  assign out_48 = {7{1'b1}};
  assign out_49 = 7'b1000000;
  assign out_50 = 7'b0100000;
  assign out_51 = 7'b0010000;
  assign out_52 = 7'b0001000;
  assign out_53 = 7'b0010000;
  assign out_54 = 7'b0100000;
  assign out_55 = 7'b1000000;
  assign out_56 = {7{1'b1}};
  assign out_57 = {7{1'b1}};
  assign out_58 = 7'b1001000;
  assign out_59 = 7'b1001000;
  assign out_60 = 7'b1001000;
  assign {out_61[6:3], out_61[1:0]} = {4'b1111, {2{out_61[2]}}};
endmodule

module SEG_DECD (
  input  b3,
  input  b2,
  input  b1,
  input  b0,
  output a,
  output b,
  output c,
  output d,
  output e,
  output f,
  output g
);

  wire n4bit_decoder_1_d0, n4bit_decoder_1_d1, n4bit_decoder_1_d2, n4bit_decoder_1_d3, n4bit_decoder_1_d4,
       n4bit_decoder_1_d5, n4bit_decoder_1_d6, n4bit_decoder_1_d7, n4bit_decoder_1_d8, n4bit_decoder_1_d9;

  _4bit_decoder u_4bit_decoder_1 (
    .a3(b3), .a2(b2), .a1(b1), .a0(b0), .D0(n4bit_decoder_1_d0), .D1(n4bit_decoder_1_d1),
    .D2(n4bit_decoder_1_d2), .D3(n4bit_decoder_1_d3), .D4(n4bit_decoder_1_d4), .D5(n4bit_decoder_1_d5),
    .D6(n4bit_decoder_1_d6), .D7(n4bit_decoder_1_d7), .D8(n4bit_decoder_1_d8), .D9(n4bit_decoder_1_d9));
  or or_1 (a, n4bit_decoder_1_d0, n4bit_decoder_1_d2, n4bit_decoder_1_d3, n4bit_decoder_1_d5, n4bit_decoder_1_d7, n4bit_decoder_1_d8, n4bit_decoder_1_d9, n4bit_decoder_1_d6);
  or or_2 (b, n4bit_decoder_1_d0, n4bit_decoder_1_d1, n4bit_decoder_1_d2, n4bit_decoder_1_d3, n4bit_decoder_1_d4, n4bit_decoder_1_d7, n4bit_decoder_1_d8, n4bit_decoder_1_d9);
  or or_3 (c, n4bit_decoder_1_d0, n4bit_decoder_1_d3, n4bit_decoder_1_d4, n4bit_decoder_1_d5, n4bit_decoder_1_d6, n4bit_decoder_1_d7, n4bit_decoder_1_d8, n4bit_decoder_1_d9, n4bit_decoder_1_d1);
  or or_4 (d, n4bit_decoder_1_d0, n4bit_decoder_1_d2, n4bit_decoder_1_d3, n4bit_decoder_1_d5, n4bit_decoder_1_d6, n4bit_decoder_1_d8);
  or or_5 (e, n4bit_decoder_1_d0, n4bit_decoder_1_d2, n4bit_decoder_1_d6, n4bit_decoder_1_d8);
  or or_6 (f, n4bit_decoder_1_d0, n4bit_decoder_1_d4, n4bit_decoder_1_d5, n4bit_decoder_1_d6, n4bit_decoder_1_d8, n4bit_decoder_1_d9);
  or or_7 (g, n4bit_decoder_1_d2, n4bit_decoder_1_d3, n4bit_decoder_1_d4, n4bit_decoder_1_d5, n4bit_decoder_1_d6, n4bit_decoder_1_d8, n4bit_decoder_1_d9);
endmodule

module H_Counter (
  input  clock,
  input  SET,
  output Lb0,
  output Rb0,
  output Lb1,
  output Rb1,
  output Lb2,
  output Rb2,
  output Lb3,
  output Rb3,
  output am_pm
);

  wire and_1_out, and_2_out, not_1_out, or_1_out, or_2_out;

  Async_4bit_counter async_4bit_counter_1 (
    .clock(and_2_out), .clear(and_1_out), .out_3(Lb0), .out_4(Lb1), .out_5(Lb2), .out_6(Lb3));
  and and_1 (and_1_out, Lb0, not_1_out, Rb1);
  T_Flip_Flop t_ff_1 (.clk(and_1_out), .T(1'b1), .Q(am_pm));  // open: Qn, preset, reset, en
  not not_1 (not_1_out, Rb3);
  or or_1 (or_1_out, clock, SET);
  or or_2 (or_2_out, and_1_out, and_2_out);
  Async_4bit_counter async_4bit_counter_2 (
    .clock(or_1_out), .clear(or_2_out), .out_3(Rb0), .out_4(Rb1), .out_5(Rb2), .out_6(Rb3));
  and and_2 (and_2_out, Rb3, Rb1);
endmodule

module R_counter (
  input  in_1,
  input  in_2,
  output Q3,
  output Q2,
  output Q1,
  output Q0,
  output overflow
);

  wire _2_qn, and_1_out, and_2_out, D1_qn, D3_qn, Do_qn, or_1_out, xor_1_out, xor_2_out, xor_3_out;

  and and_1 (and_1_out, Q0, Q1, Q2);
  and and_2 (and_2_out, Q1, Q0);
  or or_1 (or_1_out, in_1, in_2);
  xor xor_1 (xor_1_out, and_1_out, Q3);
  xor xor_2 (xor_2_out, Q1, Q0);
  and and_3 (overflow, Q3, Q3, Q1);
  xor xor_3 (xor_3_out, and_2_out, Q2);
  D_Flip_Flop D3 (.clk(or_1_out), .D(xor_1_out), .Q(Q3), .Qn(D3_qn), .reset(overflow));  // open: preset, en
  D_Flip_Flop _2 (.clk(or_1_out), .D(xor_3_out), .Q(Q2), .Qn(_2_qn), .reset(overflow));  // open: preset, en
  D_Flip_Flop D1 (.clk(or_1_out), .D(xor_2_out), .Q(Q1), .Qn(D1_qn), .reset(overflow));  // open: preset, en
  D_Flip_Flop Do (.clk(or_1_out), .D(Do_qn), .Q(Q0), .Qn(Do_qn), .reset(overflow));  // open: preset, en
endmodule

module L_counter (
  input  in_1,
  input  in_2,
  output Q3,
  output Q2,
  output Q1,
  output Q0,
  output overflow
);

  wire _2_qn, and_1_out, and_2_out, D1_qn, D3_qn, Do_qn, or_1_out, xor_1_out, xor_2_out, xor_3_out;

  and and_1 (and_1_out, Q0, Q1, Q2);
  and and_2 (and_2_out, Q1, Q0);
  or or_1 (or_1_out, in_1, in_2);
  xor xor_1 (xor_1_out, and_1_out, Q3);
  xor xor_2 (xor_2_out, Q1, Q0);
  and and_3 (overflow, Q2, Q2, Q1);
  xor xor_3 (xor_3_out, and_2_out, Q2);
  D_Flip_Flop D3 (.clk(or_1_out), .D(xor_1_out), .Q(Q3), .Qn(D3_qn), .reset(overflow));  // open: preset, en
  D_Flip_Flop _2 (.clk(or_1_out), .D(xor_3_out), .Q(Q2), .Qn(_2_qn), .reset(overflow));  // open: preset, en
  D_Flip_Flop D1 (.clk(or_1_out), .D(xor_2_out), .Q(Q1), .Qn(D1_qn), .reset(overflow));  // open: preset, en
  D_Flip_Flop Do (.clk(or_1_out), .D(Do_qn), .Q(Q0), .Qn(Do_qn), .reset(overflow));  // open: preset, en
endmodule

module Async_4bit_counter (
  input  clock,
  input  clear,
  output out_3,
  output out_4,
  output out_5,
  output out_6
);

  wire d_ff_1_qn, d_ff_2_qn, d_ff_3_qn, d_ff_4_qn, not_1_out;

  not not_1 (not_1_out, clock);
  D_Flip_Flop #(.trigger("falling")) d_ff_1 (
    .clk(not_1_out), .D(d_ff_1_qn), .Q(out_3), .Qn(d_ff_1_qn), .reset(clear));  // open: preset, en
  D_Flip_Flop #(.trigger("falling")) d_ff_2 (
    .clk(out_3), .D(d_ff_2_qn), .Q(out_4), .Qn(d_ff_2_qn), .reset(clear));  // open: preset, en
  D_Flip_Flop #(.trigger("falling")) d_ff_3 (
    .clk(out_4), .D(d_ff_3_qn), .Q(out_5), .Qn(d_ff_3_qn), .reset(clear));  // open: preset, en
  D_Flip_Flop #(.trigger("falling")) d_ff_4 (
    .clk(out_5), .D(d_ff_4_qn), .Q(out_6), .Qn(d_ff_4_qn), .reset(clear));  // open: preset, en
endmodule

module _4bit_decoder (
  input  a3,
  input  a2,
  input  a1,
  input  a0,
  output D0,
  output D1,
  output D2,
  output D3,
  output D4,
  output D5,
  output D6,
  output D7,
  output D8,
  output D9
);

  wire not_1_out, not_2_out, not_3_out, not_4_out, not_5_out, not_6_out, not_7_out, not_8_out, not_9_out,
       not_10_out, not_11_out, not_12_out, not_13_out, not_14_out, not_15_out;

  not not_1 (not_1_out, a3);
  not not_2 (not_2_out, a2);
  not not_3 (not_3_out, a1);
  not not_4 (not_4_out, a0);
  not not_5 (not_5_out, a3);
  not not_6 (not_6_out, a2);
  not not_7 (not_7_out, a1);
  not not_8 (not_8_out, a2);
  and and_1 (D2, not_8_out, a1, not_9_out);
  not not_9 (not_9_out, a0);
  not not_10 (not_10_out, a2);
  and and_2 (D3, not_10_out, a1, a0);
  not not_11 (not_11_out, a1);
  and and_3 (D4, a2, not_11_out, not_12_out);
  not not_12 (not_12_out, a0);
  not not_13 (not_13_out, a1);
  and and_4 (D5, a2, not_13_out, a0);
  and and_5 (D6, a2, a1, not_14_out);
  not not_14 (not_14_out, a0);
  and and_6 (D7, a2, a1, a0);
  and and_7 (D8, a3, not_15_out);
  not not_15 (not_15_out, a0);
  and and_8 (D9, a3, a0);
  and and_9 (D0, not_1_out, not_2_out, not_3_out, not_4_out);
  and and_10 (D1, not_5_out, not_6_out, not_7_out, a0);
endmodule
